// Logisim project Unidade Lógica e Aritmética.circ as structural Verilog: 4 circuits, main circuit ULA
module ULA (
  input  in_1,
  input  Binvert,
  input  [1:0] \Operação 
);

  wire and_1_out, clock_1_out, d_ff_1_q, full_adder_1_cout, full_adder_1_sum, n4x1_mux_1_out, or_1_out,
       registrador_1_out, registrador_2_out, xor_1_out, xor_2_out;
  wire [3:0] registrador_1__0, registrador_1__4, registrador_2__0, registrador_2__4;

  Clock clock_1 (.out(clock_1_out));
  Registrador registrador_1 (
    .Clock(clock_1_out), .In(n4x1_mux_1_out), ._7(registrador_1__4[3]), ._6(registrador_1__4[2]),
    ._5(registrador_1__4[1]), ._4(registrador_1__4[0]), ._3(registrador_1__0[3]), ._2(registrador_1__0[2]),
    ._1(registrador_1__0[1]), ._0(registrador_1__0[0]), .Out(registrador_1_out));
  Registrador registrador_2 (
    .Clock(clock_1_out), .In(in_1), ._7(registrador_2__4[3]), ._6(registrador_2__4[2]),
    ._5(registrador_2__4[1]), ._4(registrador_2__4[0]), ._3(registrador_2__0[3]), ._2(registrador_2__0[2]),
    ._1(registrador_2__0[1]), ._0(registrador_2__0[0]), .Out(registrador_2_out));
  Hex_Digit_Display hex_digit_display_1 (.value(registrador_1__4));  // open: dp
  Hex_Digit_Display hex_digit_display_2 (.value(registrador_1__0));  // open: dp
  Hex_Digit_Display hex_digit_display_3 (.value(registrador_2__4));  // open: dp
  xor xor_1 (xor_1_out, registrador_2_out, Binvert);
  Hex_Digit_Display hex_digit_display_4 (.value(registrador_2__0));  // open: dp
  and and_1 (and_1_out, registrador_1_out, registrador_2_out);
  or or_1 (or_1_out, registrador_1_out, registrador_2_out);
  xor xor_2 (xor_2_out, registrador_1_out, registrador_2_out);
  Full_Adder full_adder_1 (
    .A(registrador_1_out), .B(xor_1_out), .Cin(d_ff_1_q), .Sum(full_adder_1_sum), .Cout(full_adder_1_cout));
  D_Flip_Flop d_ff_1 (.clk(clock_1_out), .D(full_adder_1_cout), .Q(d_ff_1_q));  // open: Qn, preset, en, reset
  _4x1_Mux u_4x1_mux_1 (
    .\Operação (\Operação ), .In0(and_1_out), .In1(or_1_out), .In2(xor_2_out), .In3(full_adder_1_sum),
    .Out(n4x1_mux_1_out));
endmodule

module _4x1_Mux (
  input  [1:0] \Operação ,
  input  In0,
  input  In1,
  input  In2,
  input  In3,
  output Out
);

  wire and_1_out, and_2_out, and_3_out, and_4_out, not_1_out, not_2_out;

  not not_1 (not_1_out, \Operação [0]);
  not not_2 (not_2_out, \Operação [1]);
  and and_1 (and_1_out, \Operação [0], \Operação [1], In0);
  and and_2 (and_2_out, \Operação [0], not_2_out, In1);
  and and_3 (and_3_out, not_1_out, \Operação [1], In2);
  and and_4 (and_4_out, not_1_out, not_2_out, In3);
  or or_1 (Out, and_1_out, and_2_out, and_3_out, and_4_out);
endmodule

module Full_Adder (
  input  A,
  input  B,
  input  Cin,
  output Sum,
  output Cout
);

  wire and_1_out, and_2_out, xor_1_out;

  xor xor_1 (xor_1_out, A, B);
  and and_1 (and_1_out, Cin, xor_1_out);
  and and_2 (and_2_out, A, B);
  xor xor_2 (Sum, xor_1_out, Cin);
  or or_1 (Cout, and_1_out, and_2_out);
endmodule

module Registrador (
  input  Clock,
  input  In,
  output Out,
  output _7,
  output _6,
  output _5,
  output _4,
  output _3,
  output _2,
  output _1,
  output _0
);

  D_Flip_Flop d_ff_1 (.clk(Clock), .D(In), .Q(_7));  // open: Qn, preset, en, reset
  D_Flip_Flop d_ff_2 (.clk(Clock), .D(_7), .Q(_6));  // open: Qn, preset, en, reset
  D_Flip_Flop d_ff_3 (.clk(Clock), .D(_6), .Q(_5));  // open: Qn, preset, en, reset
  D_Flip_Flop d_ff_4 (.clk(Clock), .D(_5), .Q(_4));  // open: Qn, preset, en, reset
  D_Flip_Flop d_ff_5 (.clk(Clock), .D(_4), .Q(_3));  // open: Qn, preset, en, reset
  D_Flip_Flop d_ff_6 (.clk(Clock), .D(_3), .Q(_2));  // open: Qn, preset, en, reset
  D_Flip_Flop d_ff_7 (.clk(Clock), .D(_2), .Q(_1));  // open: Qn, preset, en, reset
  D_Flip_Flop d_ff_8 (.clk(Clock), .D(_1), .Q(_0));  // open: Qn, preset, en, reset

  assign Out = _0;
endmodule
